# Fritzing sketch Pico_sensors_wiring (saved by Fritzing 0.9.10b)
breadboards: 1

parts:
  Mod1 = Raspberry Pi Pico
  U1 = POT_SWITCH [knob_status=50% power=0.5W package=pot_pth]
  J1 = Basic Force Sensing Resistor (FSR) [package=THT]
  R1 = Resistor [tolerance=±5% resistance=15k package="1206 [SMD]"]
  U2 = HALL-EFFECT [package=sc70]
  S1 = Round Pushbutton [mn=BLUE part_number=BLUE]
  S2 = Round Pushbutton
  S3 = Round Pushbutton
  S4 = Round Pushbutton

nets:
  N1: Mod1.pin_3, Mod1.pin_8, Mod1.pin_13, Mod1.pin_18, Mod1.pin_23, Mod1.pin_28, Mod1.pin_33, Mod1.pin_38, Mod1.pin_42, U1.G$1_A, R1.Pin_1, U2.VCC, S1.leg1, S2.leg1, S3.leg1, S4.leg1
  N2: Mod1.pin_14, S1.leg0
  N3: Mod1.pin_15, S2.leg0
  N4: Mod1.pin_16, S3.leg0
  N5: Mod1.pin_17, S4.leg0
  N6: Mod1.pin_21, U2.GND
  N7: Mod1.pin_31, U1.G$2_1
  N8: Mod1.pin_32, J1.pin_1, R1.Pin_0
  N9: Mod1.pin_36, U1.G$1_E, J1.pin_0, U2.OUT

custom parts:
  Raspberry Pi Pico: Raspberry Pi Pico. Based around the RP2040 microcontroller the Pico is a low cost microcontroller device bringing Raspberry Pi quality, cost, and easy of use to the microcontroller space. Jan 2021, Split part in to two versions: tht (this one) and SMD. This one will drill holes for a .1 in header in pcb to allow plugging in the module as well as providing pads to solder the module to the top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
